# Fritzing sketch Circuit (saved by Fritzing 0.9.4)
breadboards: 1

parts:
  Raspberry_Pi_1 = Raspberry Pi 3 [part_number=RPI-3-V1.2]
  VCC1 = 4 x AAA Battery Mount
  Part1 = Solid State High Level Relay Module [package=relay]
  M1 = DC Motor
  Part3 = Adafruit 4-channel I2C-safe Bi-directional Logic Level Converter [part_number="Adafruit #757"]

nets:
  N1: Raspberry_Pi_1.3v3, Part3.LV
  N2: Raspberry_Pi_1.GPIO3, Part3.A1
  GND: Raspberry_Pi_1.GND, Part1.DC-, Part3.GND
  N3: Raspberry_Pi_1.5V, Part1.DC+, Part3.HV
  N4: VCC1.-, Part1.A1
  N5: Part1.B1, M1.pin_2
  N6: Part1.CH1, Part3.B1

notes:
  5v relay module

custom parts:
  Solid State High Level Relay Module: 5V Omron solid state relay 240V 2A output with resistance fuse.
  Adafruit 4-channel I2C-safe Bi-directional Logic Level Converter: Because the Arduino (and Basic Stamp) are 5V devices, and most modern sensors, displays, flash cards and modes are 3.3V-only, many makers find that they need to perform level shifting/conversion to protect the 3.3V device from 5V. We do have some other handy level shifters in the shop, from the DIP 74LVC245 to the fancy bi-directional TXB0108. However, neither of these are happy to work with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
